# Fritzing sketch useless (saved by Fritzing 0.8.5b)
breadboards: 1

parts:
  Part1 = Arduino Uno (Rev3)
  J1 = Basic Servo
  U1 = RELAY-SOLIDSTATE [package=relay-s108t02]
  U2 = LIPO-110mAh [package=lipo-110]
  S2 = Toggle Switch [package=THT]
  R1 = Resistor [tolerance=±5% resistance=220 package=THT]
  D1 = Diode [package=diode-1n4148]
  D2 = Diode [package=diode-1n4148]

nets:
  N1: Part1.D9_PWM, J1.pulse
  N2: Part1.D2, R1.Pin_1
  N3: Part1.D3_PWM, U1.+
  5V: Part1.5V, J1.vcc
  GND: Part1.GND, J1.gnd, U1.-, U2.-
  N4: Part1.VIN, D1.C, D2.C
  N5: U1.T1, U2.+, S2.COM
  N6: U1.T2, D2.A
  N7: S2.L2, R1.Pin_0, D1.A
